# Fritzing sketch circuit-diagram (saved by Fritzing 0.9.3b)

parts:
  Part1 = Espruino
  Part2 = Soil Moisture Sensor
  DS1 = DS18B20 1-Wire Temperature Sensor [part_number=DS18B20]
  R1 = Resistor [tolerance=±10% resistance=4.7k package="1206 [SMD]"]

nets:
  N1: Part1.A1, DS1.DQ, R1.Pin_1
  N2: Part1.3.3#18, DS1.VDD, R1.Pin_0
  N3: Part1.GND#20, DS1.GND
  N4: Part1.C5, Part2.SIG
  N5: Part1.3.3#38, Part2.VCC
  N6: Part1.GND#40, Part2.GND

notes:
  On board LED Status values:
  ==============
  LED1 - Green - Temp in range
  LED2 - Red - Temp outside range
  LED3 - Blue - Low moisture

custom parts:
  Espruino: Espruino is an Interactive JavaScript interpreter for Microcontrollers, so you can program them quickly and easily. The Espruino Board on KickStarter is a specially designed computer with Espruino software pre-installed. It complements the Espruino software with masses of functionality and great battery life.
